// Logisim project NOT_gate.circ as structural Verilog
module main (
  input  a,
  output y
);

  NOT_gate not_gate_1 (.a(a), .y(y));
endmodule

// VHDL entity NOT_gate, as the project stores it:
LIBRARY ieee;
USE ieee.std_logic_1164.ALL;

ENTITY NOT_gate IS
    PORT (
        a : IN STD_LOGIC;
        y : OUT STD_LOGIC
    );
END NOT_gate;

ARCHITECTURE Behavioral OF NOT_gate IS
BEGIN
    y <= NOT a;
END Behavioral;
