// Logisim project sevensegment_code.circ as structural Verilog
module main (
  input  en,
  input  [12:0] vt,
  input  in_3
);

  wire [6:0] sevensegment_1_seg;

  sevensegment sevensegment_1 (.en(en), .vt(vt), .seg(sevensegment_1_seg));
  _7_Segment_Display u_7_segment_display_1 (
    .g(sevensegment_1_seg[1]), .f(sevensegment_1_seg[0]), .a(sevensegment_1_seg[6]),
    .b(sevensegment_1_seg[5]), .e(sevensegment_1_seg[2]), .d(sevensegment_1_seg[3]),
    .c(sevensegment_1_seg[4]), .dp(in_3));
endmodule

// VHDL entity sevensegment, as the project stores it:
LIBRARY ieee;
USE ieee.std_logic_1164.ALL;

ENTITY sevensegment IS
    PORT (
        en  : IN  STD_LOGIC;
        vt  : IN  STD_LOGIC_VECTOR(12 DOWNTO 0);
        seg : OUT STD_LOGIC_VECTOR(6 DOWNTO 0)
    );
END sevensegment;

ARCHITECTURE Behavioral OF sevensegment IS
BEGIN

    PROCESS(en, vt)
        VARIABLE count : INTEGER RANGE 0 TO 13;
    BEGIN

        IF en = '0' THEN
            seg <= "ZZZZZZZZ";

        ELSE
            count := 0;

            FOR i IN vt'RANGE LOOP
                IF vt(i) = '1' THEN
                    count := count + 1;
                END IF;
            END LOOP;

            CASE count IS
                WHEN 0  => seg <= "1111110";
                WHEN 1  => seg <= "0110000";
                WHEN 2  => seg <= "1101101";
                WHEN 3  => seg <= "1111001";
                WHEN 4  => seg <= "0110011";
                WHEN 5  => seg <= "1011011";
                WHEN 6  => seg <= "1011111";
                WHEN 7  => seg <= "1110000";
                WHEN 8  => seg <= "1111111";
                WHEN 9  => seg <= "1111011";
                WHEN 10 => seg <= "1110111"; -- A
                WHEN 11 => seg <= "0011111"; -- b
                WHEN 12 => seg <= "1001110"; -- C
                WHEN 13 => seg <= "0111101"; -- d
                WHEN OTHERS => seg <= "0000000";
            END CASE;

        END IF;

    END PROCESS;

END Behavioral;
