// Logisim project d_flip_flop.circ as structural Verilog
module main (
  input  in_1,
  input  in_2,
  output out_3,
  output out_4
);

  wire nand_1_out, nand_2_out, nand_3_out, nand_4_out, nand_5_out, nand_6_out, not_1_out, not_2_out,
       not_3_out, not_4_out;

  not not_1 (not_1_out, in_2);
  not not_2 (not_2_out, in_1);
  nand nand_1 (nand_1_out, in_1, not_1_out);
  nand nand_2 (nand_2_out, not_1_out, not_2_out);
  not not_3 (not_3_out, not_1_out);
  nand nand_3 (nand_3_out, nand_1_out, nand_4_out);
  nand nand_4 (nand_4_out, nand_3_out, nand_2_out);
  not not_4 (not_4_out, nand_3_out);
  nand nand_5 (nand_5_out, nand_3_out, not_3_out);
  nand nand_6 (nand_6_out, not_3_out, not_4_out);
  nand nand_7 (out_3, nand_5_out, out_4);
  nand nand_8 (out_4, out_3, nand_6_out);
endmodule

// VHDL entity D_FLIPFLOP, as the project stores it:
library IEEE;
use IEEE.STD_LOGIC_1164.ALL;

entity D_FLIPFLOP is
    Port (
        D   : in STD_LOGIC;
        clk : in STD_LOGIC;
        Q   : out STD_LOGIC
    );
end D_FLIPFLOP;

architecture Behavioral of D_FLIPFLOP is
    signal q_int : STD_LOGIC := '0';
begin

    process(clk)
    begin
        if rising_edge(clk) then
            q_int <= D;
        end if;
    end process;

    Q <= q_int;

end Behavioral;
