// Logisim project d_latch.circ as structural Verilog
module main (
  input  in_1,
  input  in_2,
  input  in_3,
  input  in_4,
  output out_5,
  output out_6,
  output out_7
);

  wire nand_1_out, nand_2_out, not_1_out;

  not not_1 (not_1_out, in_1);
  nand nand_1 (nand_1_out, in_1, in_2);
  nand nand_2 (nand_2_out, in_2, not_1_out);
  nand nand_3 (out_5, nand_1_out, out_6);
  nand nand_4 (out_6, out_5, nand_2_out);
  D_LATCH d_latch_1 (.D(in_3), .en(in_4), .Q(out_7));
endmodule

// VHDL entity D_LATCH, as the project stores it:
library IEEE;
use IEEE.STD_LOGIC_1164.ALL;

entity D_LATCH is
    Port (
        D  : in STD_LOGIC;
        en : in STD_LOGIC;
        Q  : out STD_LOGIC
    );
end D_LATCH;

architecture Behavioral of D_LATCH is
    signal q_int : STD_LOGIC := '0';
begin

    process(D, en)
    begin
        if en = '1' then
            q_int <= D;
        end if;
    end process;

    Q <= q_int;

end Behavioral;
