// Logisim project jk_flipflop.circ as structural Verilog
module main (
  input  J,
  input  CLK,
  input  in_3,
  input  K,
  output out_5,
  output out_6
);

  wire nand_1_out, nand_2_out;

  nand nand_1 (nand_1_out, out_6, J, CLK);
  nand nand_2 (nand_2_out, CLK, K, out_5);
  nand nand_3 (out_5, nand_1_out, out_6);
  nand nand_4 (out_6, out_5, in_3, nand_2_out);
endmodule

// VHDL entity JK_FLIPFLOP, as the project stores it:
library IEEE;
use IEEE.STD_LOGIC_1164.ALL;

entity JK_FLIPFLOP is
    Port (
        clk : in STD_LOGIC;
        j   : in STD_LOGIC;
        k   : in STD_LOGIC;
        q   : out STD_LOGIC
    );
end JK_FLIPFLOP;

architecture bhv of JK_FLIPFLOP is
    signal q_internal : STD_LOGIC := '0';
begin

    q <= q_internal;

    process(clk)
    begin
        if rising_edge(clk) then

            if (j = '1' and k = '0') then
                q_internal <= '1';

            elsif (j = '0' and k = '1') then
                q_internal <= '0';

            elsif (j = '1' and k = '1') then
                q_internal <= not q_internal;

            end if;

        end if;
    end process;

end bhv;
